# Fritzing sketch BWM (saved by Fritzing 0.9.3b)
breadboards: 1

parts:
  Part1 = Arduino Uno (Rev3)
  R1 = Photocell (LDR) [package=THT]
  R2 = Photocell (LDR) [package=THT]  # not connected
  LED1 = LED - 5mm [color="Red (633nm)" package="5 mm [THT]"]  # not connected
  LED2 = LED - 5mm [color="Red (633nm)" package="5 mm [THT]"]
  V1 = DC Power [voltage=5]  # not connected
  R3 = Resistor [tolerance=±5% resistance=6.8k package=THT]
  R4 = Resistor [tolerance=±5% resistance=6.8k package=THT]
  R5 = Resistor [tolerance=±5% resistance=4.7k package=THT]
  R6 = Resistor [tolerance=±5% resistance=4.7k package=THT]
  Power_plug1 = Power plug

nets:
  N1: Part1.D2, R3.Pin_0, R5.Pin_1
  N2: Part1.D3_PWM, R4.Pin_1, R6.Pin_0
  GND: Part1.GND, R1.pin_1, LED2.cathode, R5.Pin_0, R6.Pin_1, Power_plug1.GND
  N3: R1.pin_0, LED2.anode, Power_plug1.VCC

notes:
  Transmitter
  Reciver
  12V
  LB 1
  LB 2
  Spgteiler:
  12V-6.8kOhm -Ans 5V- 4.7kOhm-GND
